# Fritzing sketch Lesson1_Lesson2_Sketch (saved by Fritzing 0.9.6b)
breadboards: 1

parts:
  Part1 = Arduino Uno (Rev3) - ICSP
  R1 = Resistor [tolerance=±5% resistance=470 package="0402 [SMD]"]
  R2 = Resistor [tolerance=±5% resistance=470 package="0402 [SMD]"]
  LED1 = smd LED [color="Red (633nm)" package="0603 [SMD]"]
  LED2 = smd LED [color="Blue (430nm)" package="0603 [SMD]"]

nets:
  N1: Part1.D4, R1.Pin_0
  N2: Part1.D5_PWM, R2.Pin_0
  N3: Part1.GND, LED1.cathode, LED2.cathode
  N4: R1.Pin_1, LED1.anode
  N5: R2.Pin_1, LED2.anode

notes:
  Blue wire from Pin 4 To A6
  Yellow wire from Pin 5 to A21
  R1 and R2 are 470R "Yellow , Purple, Brown
  LED1 , LED2 Kathod to ground which is Y1 to Y29
  Anode Led1 to J6 and Anode LED2 to J21
  MD Harrington
  Date 04/02/2024
  Use this layout for lesson 1 and lesson 2
  LED1
  LED 2
  R1
  R2
